// Logisim project tab_dec_iso.circ as structural Verilog: 1 circuit, main circuit main
module main (
  input  in0,
  input  in1,
  output out0,
  output out1,
  output out2,
  output out3
);

  wire not_1_out, not_2_out;

  not not_1 (not_1_out, in0);
  not not_2 (not_2_out, in1);
  and and_1 (out0, not_1_out, not_2_out);
  and and_2 (out1, in0, not_2_out);
  and and_3 (out2, not_1_out, in1);
  and and_4 (out3, in0, in1);
endmodule
