// Logisim project tab_iso.circ as structural Verilog: 1 circuit, main circuit main
module main (
  input  in_1,
  input  in1,
  input  in0,
  output out0,
  output out1
);

  wire and_1_out, and_2_out, and_3_out, and_4_out, and_5_out, and_6_out, and_7_out, not_1_out, not_2_out,
       not_3_out;

  not not_1 (not_1_out, in0);
  not not_2 (not_2_out, in0);
  not not_3 (not_3_out, in0);
  and and_1 (and_1_out, not_1_out, not_2_out, in0);
  and and_2 (and_2_out, not_1_out, in0, not_3_out);
  and and_3 (and_3_out, in0, not_2_out, not_3_out);
  and and_4 (and_4_out, in0, in0, in0);
  and and_5 (and_5_out, in0, in0);
  and and_6 (and_6_out, in0, in0);
  and and_7 (and_7_out, in0, in0);
  or or_1 (out0, and_1_out, and_2_out, and_3_out, and_4_out);
  or or_2 (out1, and_5_out, and_6_out, and_7_out);

  assign in1 = in0;
  assign in_1 = in0;

  // Notes on the sheet:
  //        in2
endmodule
